// Logisim project TallerLogica-Combinatorios-individual.circ as structural Verilog: 11 circuits, main circuit verificador
module sumador_simple (
  input  A,
  input  B,
  output S,
  output Cout
);

  xor xor_1 (S, A, B);
  and and_1 (Cout, A, B);
endmodule

module sumador_completo (
  input  Cin,
  input  A,
  input  B,
  output S,
  output Cout
);

  wire sumador_simple_1_cout, sumador_simple_1_s, sumador_simple_2_cout;

  sumador_simple sumador_simple_1 (.A(A), .B(B), .S(sumador_simple_1_s), .Cout(sumador_simple_1_cout));
  sumador_simple sumador_simple_2 (.A(Cin), .B(sumador_simple_1_s), .S(S), .Cout(sumador_simple_2_cout));
  or or_1 (Cout, sumador_simple_1_cout, sumador_simple_2_cout);
endmodule

module sumador_4 (
  input  Cin,
  input  [3:0] A,
  input  [3:0] B,
  output [3:0] S,
  output Cout
);

  wire sumador_completo_1_cout, sumador_completo_2_cout, sumador_completo_3_cout;

  sumador_completo sumador_completo_1 (.Cin(Cin), .A(A[0]), .B(B[0]), .S(S[0]), .Cout(sumador_completo_1_cout));
  sumador_completo sumador_completo_2 (
    .Cin(sumador_completo_1_cout), .A(A[1]), .B(B[1]), .S(S[1]), .Cout(sumador_completo_2_cout));
  sumador_completo sumador_completo_3 (
    .Cin(sumador_completo_2_cout), .A(A[2]), .B(B[2]), .S(S[2]), .Cout(sumador_completo_3_cout));
  sumador_completo sumador_completo_4 (.Cin(sumador_completo_3_cout), .A(A[3]), .B(B[3]), .S(S[3]), .Cout(Cout));
  Hex_Digit_Display hex_digit_display_1 (.value(S));  // open: dp
endmodule

module comparador_cero (
  input  [3:0] A,
  output Z
);

  nor nor_1 (Z, A[0], A[1], A[2], A[3]);
endmodule

module sumador_flags (
  input  [3:0] A,
  input  [3:0] B,
  input  Cin,
  output N,
  output [3:0] S,
  output Z,
  output C,
  output V
);

  wire xor_1_out, xor_2_out;

  xor xor_1 (xor_1_out, A[3], B[3]);
  xor xor_2 (xor_2_out, xor_1_out, N);
  sumador_4 sumador_4_1 (.Cin(Cin), .A(A), .B(B), .S({N, S[2:0]}), .Cout(C));
  Hex_Digit_Display hex_digit_display_1 (.value({N, S[2:0]}));  // open: dp
  comp_overflow comp_overflow_1 (.c3(C), .a3(xor_2_out), .b3(xor_2_out), .O(V));
  comparador_cero comparador_cero_1 (.A({N, S[2:0]}), .Z(Z));

  assign S[3] = N;

  // Other names for the same wires on the sheet: A_t[3:0] = A; A_MSb = A[3]; B_t[3:0] = B; B_MSb = B[3]
endmodule

module incrementador_4 (
  input  [3:0] A,
  output [3:0] S
);

  sumador_4 sumador_4_1 (.A(A), .B(4'b0001), .S(S));  // open: Cin, Cout
  Hex_Digit_Display hex_digit_display_1 (.value(S));  // open: dp
endmodule

module inversor_4 (
  input  [3:0] A,
  input  INV,
  output [3:0] S
);

  wire [3:0] incrementador_4_1_s, not_1_out;

  not not_1 (not_1_out[0], A[0]);
  not not_2 (not_1_out[1], A[1]);
  not not_3 (not_1_out[2], A[2]);
  not not_4 (not_1_out[3], A[3]);
  Multiplexer #(.width(4)) multiplexer_1 (.in0(A), .in1(incrementador_4_1_s), .out(S), .sel(INV));
  incrementador_4 incrementador_4_1 (.A(not_1_out), .S(incrementador_4_1_s));
  Hex_Digit_Display hex_digit_display_1 (.value(S));  // open: dp
endmodule

module ALU (
  input  [1:0] OP,
  input  [3:0] A,
  input  [3:0] B,
  output N,
  output Z,
  output V,
  output C,
  output [3:0] out_8
);

  wire comparador_cero_1_z, Cout, multiplexer_3_out, not_1_out, OP_B2, V_R, V_S, xor_1_out, xor_2_out,
       xor_3_out;
  wire [3:0] B_I, multiplexer_1_out, S_AND, S_OR, S_SUMA;

  and and_1 (S_AND[3], A[3], B[3]);
  xor xor_1 (xor_1_out, A[3], multiplexer_1_out[3]);
  Multiplexer #(.width(4)) multiplexer_1 (.in0(B), .in1(B_I), .out(multiplexer_1_out), .sel(OP_B2));
  and and_2 (S_AND[2], A[2], B[2]);
  xor xor_2 (xor_2_out, xor_1_out, N);
  and and_3 (S_AND[1], A[1], B[1]);
  and and_4 (S_AND[0], A[0], B[0]);
  sumador_4 sumador_4_1 (.A(A), .B(B_I), .S(S_SUMA), .Cout(Cout));  // open: Cin
  xor xor_3 (xor_3_out, OP[1], OP[0]);
  not not_1 (not_1_out, Cout);
  comparador_cero comparador_cero_1 (.A(B), .Z(comparador_cero_1_z));
  or or_1 (S_OR[3], A[3], B[3]);
  and and_5 (OP_B2, OP[0], xor_3_out);
  Multiplexer #(.select(2), .width(4)) multiplexer_2 (
    .in0(S_SUMA), .in1(S_SUMA), .in2(S_AND), .in3(S_OR), .out({N, out_8[2:0]}), .sel(OP));
  comp_overflow comp_overflow_1 (.c3(Cout), .a3(xor_2_out), .b3(xor_2_out), .O(V_S));
  Multiplexer multiplexer_3 (.in0(not_1_out), .in1(1'b0), .out(multiplexer_3_out), .sel(comparador_cero_1_z));
  or or_2 (S_OR[2], A[2], B[2]);
  Multiplexer #(.select(2)) multiplexer_4 (.in0(V_S), .in1(V_R), .in2(1'b0), .in3(1'b0), .out(V), .sel(OP));
  Multiplexer #(.select(2)) multiplexer_5 (
    .in0(Cout), .in1(multiplexer_3_out), .in2(1'b0), .in3(1'b0), .out(C), .sel(OP));
  or or_3 (S_OR[1], A[1], B[1]);
  or or_4 (S_OR[0], A[0], B[0]);
  inversor_4 inversor_4_1 (.A(B), .INV(OP_B2), .S(B_I));
  Hex_Digit_Display hex_digit_display_1 (.value({N, out_8[2:0]}));  // open: dp
  comparador_cero comparador_cero_2 (.A({N, out_8[2:0]}), .Z(Z));
  overflow_resta overflow_resta_1 (.V_in(V_S), .B(B), .V_out(V_R));

  assign out_8[3] = N;

  // Other names for the same wires on the sheet: S[3:0] = {N, out_8[2:0]}
endmodule

module verificador (
  output [3:0] out_1,
  output [3:0] out_2,
  output [1:0] out_3,
  output halt,
  output N,
  output Z,
  output V,
  output C,
  output [3:0] res
);

  wire clock_1_out;

  Clock clock_1 (.out(clock_1_out));
  Counter #(.max('h3ff), .width(10)) counter_1 (
    .clk(clock_1_out), .carry(halt), .Q({out_3, out_2, out_1}));  // open: clr, load, up, count, D
  ALU alu_1 (.OP(out_3), .A(out_1), .B(out_2), .N(N), .Z(Z), .V(V), .C(C), .out_8(res));
endmodule

module overflow_resta (
  input  V_in,
  input  [3:0] B,
  output V_out
);

  wire comparador_cero_1_z, not_2_out;
  wire [3:3] not_1_out;

  not not_1 (not_1_out[3], B[3]);
  not not_2 (not_2_out, V_in);
  comparador_cero comparador_cero_1 (.A({not_1_out[3], B[2:0]}), .Z(comparador_cero_1_z));
  Multiplexer multiplexer_1 (.in0(V_in), .in1(not_2_out), .out(V_out), .sel(comparador_cero_1_z));
endmodule

module comp_overflow (
  input  c3,
  input  a3,
  input  b3,
  output O
);

  wire not_1_out, xor_1_out, xor_2_out;

  xor xor_1 (xor_1_out, c3, a3);
  not not_1 (not_1_out, xor_2_out);
  xor xor_2 (xor_2_out, a3, b3);
  and and_1 (O, xor_1_out, not_1_out);
endmodule
